// Logisim project RegisterFile.circ as structural Verilog
module main (
  input  glbRst,
  input  [3:0] RS1,
  input  [3:0] RS2,
  output [15:0] RS1VAL,
  output [15:0] RS2VAL
);

  wire decoder_1_out0, decoder_1_out1, decoder_1_out2, decoder_1_out3, decoder_1_out4, decoder_1_out5,
       decoder_1_out6, decoder_1_out7, decoder_1_out8, decoder_1_out9, decoder_1_out10, decoder_1_out11,
       decoder_1_out12, decoder_1_out13, decoder_1_out14, decoder_1_out15;
  wire [15:0] r0, r1, r2, r3, r4, r5, r6, r7, r8, r9, r10, r11, r12, r13, r14, r15;

  Decoder #(.select(4)) decoder_1 (
    .out0(decoder_1_out0), .out1(decoder_1_out1), .out2(decoder_1_out2), .out3(decoder_1_out3),
    .out4(decoder_1_out4), .out5(decoder_1_out5), .out6(decoder_1_out6), .out7(decoder_1_out7),
    .out8(decoder_1_out8), .out9(decoder_1_out9), .out10(decoder_1_out10), .out11(decoder_1_out11),
    .out12(decoder_1_out12), .out13(decoder_1_out13), .out14(decoder_1_out14), .out15(decoder_1_out15));  // open: sel, en
  _16bitRegister u_16bitregister_1 (.we(decoder_1_out0), .rst(glbRst), .dataOut(r0));  // open: dataIn, clk
  _16bitRegister u_16bitregister_2 (.we(decoder_1_out1), .rst(glbRst), .dataOut(r1));  // open: dataIn, clk
  _16bitRegister u_16bitregister_3 (.we(decoder_1_out2), .rst(glbRst), .dataOut(r2));  // open: dataIn, clk
  _16bitRegister u_16bitregister_4 (.we(decoder_1_out3), .rst(glbRst), .dataOut(r3));  // open: dataIn, clk
  _16bitRegister u_16bitregister_5 (.we(decoder_1_out4), .rst(glbRst), .dataOut(r4));  // open: dataIn, clk
  _16bitRegister u_16bitregister_6 (.we(decoder_1_out5), .rst(glbRst), .dataOut(r5));  // open: dataIn, clk
  _16bitRegister u_16bitregister_7 (.we(decoder_1_out6), .rst(glbRst), .dataOut(r6));  // open: dataIn, clk
  _16bitRegister u_16bitregister_8 (.we(decoder_1_out7), .rst(glbRst), .dataOut(r7));  // open: dataIn, clk
  _16bitRegister u_16bitregister_9 (.we(decoder_1_out8), .rst(glbRst), .dataOut(r8));  // open: dataIn, clk
  _16bitRegister u_16bitregister_10 (.we(decoder_1_out9), .rst(glbRst), .dataOut(r9));  // open: dataIn, clk
  _16bitRegister u_16bitregister_11 (.we(decoder_1_out10), .rst(glbRst), .dataOut(r10));  // open: dataIn, clk
  _16bitRegister u_16bitregister_12 (.we(decoder_1_out11), .rst(glbRst), .dataOut(r11));  // open: dataIn, clk
  _16bitRegister u_16bitregister_13 (.we(decoder_1_out12), .rst(glbRst), .dataOut(r12));  // open: dataIn, clk
  _16bitRegister u_16bitregister_14 (.we(decoder_1_out13), .rst(glbRst), .dataOut(r13));  // open: dataIn, clk
  _16bitRegister u_16bitregister_15 (.we(decoder_1_out14), .rst(glbRst), .dataOut(r14));  // open: dataIn, clk
  _16bitRegister u_16bitregister_16 (.we(decoder_1_out15), .rst(glbRst), .dataOut(r15));  // open: dataIn, clk
  Multiplexer #(.select(4), .width(16)) multiplexer_1 (
    .in0(r0), .in1(r1), .in2(r2), .in3(r3), .in4(r4), .in5(r5), .in6(r6), .in7(r7), .in8(r8), .in9(r9),
    .in10(r10), .in11(r11), .in12(r12), .in13(r13), .in14(r14), .in15(r15), .out(RS1VAL), .sel(RS1));  // open: en
  Multiplexer #(.select(4), .width(16)) multiplexer_2 (
    .in0(r0), .in1(r1), .in2(r2), .in3(r3), .in4(r4), .in5(r5), .in6(r6), .in7(r7), .in8(r8), .in9(r9),
    .in10(r10), .in11(r11), .in12(r12), .in13(r13), .in14(r14), .in15(r15), .out(RS2VAL), .sel(RS2));  // open: en
endmodule

module _16bitRegister (
  input  clk,
  input  we,
  input  rst,
  input  [15:0] dataIn,
  output [15:0] dataOut
);

  wire and_1_out, not_1_out;

  and and_1 (and_1_out, clk, we);
  not not_1 (not_1_out, rst);
  D_Flip_Flop d_ff_1 (.clk(and_1_out), .D(dataIn[0]), .Q(dataOut[0]), .reset(not_1_out));  // open: Qn, preset, en
  D_Flip_Flop d_ff_2 (.clk(and_1_out), .D(dataIn[1]), .Q(dataOut[1]), .reset(not_1_out));  // open: Qn, preset, en
  D_Flip_Flop d_ff_3 (.clk(and_1_out), .D(dataIn[2]), .Q(dataOut[2]), .reset(not_1_out));  // open: Qn, preset, en
  D_Flip_Flop d_ff_4 (.clk(and_1_out), .D(dataIn[3]), .Q(dataOut[3]), .reset(not_1_out));  // open: Qn, preset, en
  D_Flip_Flop d_ff_5 (.clk(and_1_out), .D(dataIn[4]), .Q(dataOut[4]), .reset(not_1_out));  // open: Qn, preset, en
  D_Flip_Flop d_ff_6 (.clk(and_1_out), .D(dataIn[5]), .Q(dataOut[5]), .reset(not_1_out));  // open: Qn, preset, en
  D_Flip_Flop d_ff_7 (.clk(and_1_out), .D(dataIn[6]), .Q(dataOut[6]), .reset(not_1_out));  // open: Qn, preset, en
  D_Flip_Flop d_ff_8 (.clk(and_1_out), .D(dataIn[7]), .Q(dataOut[7]), .reset(not_1_out));  // open: Qn, preset, en
  D_Flip_Flop d_ff_9 (.clk(and_1_out), .D(dataIn[8]), .Q(dataOut[8]), .reset(not_1_out));  // open: Qn, preset, en
  D_Flip_Flop d_ff_10 (.clk(and_1_out), .D(dataIn[9]), .Q(dataOut[9]), .reset(not_1_out));  // open: Qn, preset, en
  D_Flip_Flop d_ff_11 (.clk(and_1_out), .D(dataIn[10]), .Q(dataOut[10]), .reset(not_1_out));  // open: Qn, preset, en
  D_Flip_Flop d_ff_12 (.clk(and_1_out), .D(dataIn[11]), .Q(dataOut[11]), .reset(not_1_out));  // open: Qn, preset, en
  D_Flip_Flop d_ff_13 (.clk(and_1_out), .D(dataIn[12]), .Q(dataOut[12]), .reset(not_1_out));  // open: Qn, preset, en
  D_Flip_Flop d_ff_14 (.clk(and_1_out), .D(dataIn[13]), .Q(dataOut[13]), .reset(not_1_out));  // open: Qn, preset, en
  D_Flip_Flop d_ff_15 (.clk(and_1_out), .D(dataIn[14]), .Q(dataOut[14]), .reset(not_1_out));  // open: Qn, preset, en
  D_Flip_Flop d_ff_16 (.clk(and_1_out), .D(dataIn[15]), .Q(dataOut[15]), .reset(not_1_out));  // open: Qn, preset, en
endmodule
