// Logisim project hw4.circ as structural Verilog: 12 circuits, main circuit main
module main (
  input  Reset,
  input  WE,
  input  Rwd,
  input  [2:0] ALUop,
  input  DMwe,
  input  ALUinB,
  input  [2:0] shamt,
  input  Rdst,
  input  [2:0] rd,
  input  [2:0] rs,
  input  [2:0] rt,
  input  [5:0] immediate
);

  wire clock_1_out, not_1_out;
  wire [2:0] multiplexer_1_out;
  wire [15:0] ALU_result, BitExtender_extended, multiplexer_2_out, multiplexer_3_out, PC_dataout,
       pcincrement_1_pcout, RegisterFile_rs1val, RegisterFile_rs2val, rom_1_data, transistor_1_out;

  _16bitRegister PC (
    .dataIn(pcincrement_1_pcout), .clk(clock_1_out), .we(clock_1_out), .dataOut(PC_dataout));  // open: rst
  PCIncrement pcincrement_1 (.PCIn(PC_dataout), .PCOut(pcincrement_1_pcout));
  ROM #(.addrWidth(16), .dataWidth(16)) rom_1 (.addr(PC_dataout), .data(rom_1_data));  // open: sel
  Clock clock_1 (.out(clock_1_out));
  // Probe on multiplexer_1_out
  Multiplexer #(.width(3)) multiplexer_1 (.in0(rd), .in1(rt), .out(multiplexer_1_out), .sel(Rdst));  // open: en
  RegisterFile RegisterFile (
    .clk(clock_1_out), .rst(Reset), .RDVAL(multiplexer_3_out), .RD(multiplexer_1_out), .WE(WE), .RS2(rs),
    .RS1(rt), .RS2VAL(RegisterFile_rs2val), .RS1VAL(RegisterFile_rs1val));
  Extender BitExtender (.extended(BitExtender_extended), .immediate(immediate));
  Multiplexer #(.width(16)) multiplexer_2 (
    .in0(RegisterFile_rs1val), .in1(BitExtender_extended), .out(multiplexer_2_out), .sel(ALUinB));  // open: en
  ALU ALU (.numA(RegisterFile_rs2val), .numB(multiplexer_2_out), .ALUop(ALUop), .shamt(shamt), .Result(ALU_result));
  Transistor #(.gate("br"), .width(16)) transistor_1 (.in(RegisterFile_rs1val), .out(transistor_1_out), .gate(DMwe));
  RAM #(.addrWidth(16), .dataWidth(16)) ram_1 (
    .addr(ALU_result), .data(transistor_1_out), .clk(clock_1_out), .ld(not_1_out));  // open: sel, clr
  not not_1 (not_1_out, DMwe);
  Multiplexer #(.width(16)) multiplexer_3 (
    .in0(ALU_result), .in1(transistor_1_out), .out(multiplexer_3_out), .sel(Rwd));  // open: en
  // Probe on multiplexer_3_out
endmodule

module _16bitRegister (
  input  clk,
  input  we,
  input  rst,
  input  [15:0] dataIn,
  output [15:0] dataOut
);

  wire and_1_out;

  and and_1 (and_1_out, clk, we);
  D_Flip_Flop d_ff_1 (.clk(and_1_out), .D(dataIn[0]), .Q(dataOut[0]), .reset(rst));  // open: Qn, preset, en
  D_Flip_Flop d_ff_2 (.clk(and_1_out), .D(dataIn[1]), .Q(dataOut[1]), .reset(rst));  // open: Qn, preset, en
  D_Flip_Flop d_ff_3 (.clk(and_1_out), .D(dataIn[2]), .Q(dataOut[2]), .reset(rst));  // open: Qn, preset, en
  D_Flip_Flop d_ff_4 (.clk(and_1_out), .D(dataIn[3]), .Q(dataOut[3]), .reset(rst));  // open: Qn, preset, en
  D_Flip_Flop d_ff_5 (.clk(and_1_out), .D(dataIn[4]), .Q(dataOut[4]), .reset(rst));  // open: Qn, preset, en
  D_Flip_Flop d_ff_6 (.clk(and_1_out), .D(dataIn[5]), .Q(dataOut[5]), .reset(rst));  // open: Qn, preset, en
  D_Flip_Flop d_ff_7 (.clk(and_1_out), .D(dataIn[6]), .Q(dataOut[6]), .reset(rst));  // open: Qn, preset, en
  D_Flip_Flop d_ff_8 (.clk(and_1_out), .D(dataIn[7]), .Q(dataOut[7]), .reset(rst));  // open: Qn, preset, en
  D_Flip_Flop d_ff_9 (.clk(and_1_out), .D(dataIn[8]), .Q(dataOut[8]), .reset(rst));  // open: Qn, preset, en
  D_Flip_Flop d_ff_10 (.clk(and_1_out), .D(dataIn[9]), .Q(dataOut[9]), .reset(rst));  // open: Qn, preset, en
  D_Flip_Flop d_ff_11 (.clk(and_1_out), .D(dataIn[10]), .Q(dataOut[10]), .reset(rst));  // open: Qn, preset, en
  D_Flip_Flop d_ff_12 (.clk(and_1_out), .D(dataIn[11]), .Q(dataOut[11]), .reset(rst));  // open: Qn, preset, en
  D_Flip_Flop d_ff_13 (.clk(and_1_out), .D(dataIn[12]), .Q(dataOut[12]), .reset(rst));  // open: Qn, preset, en
  D_Flip_Flop d_ff_14 (.clk(and_1_out), .D(dataIn[13]), .Q(dataOut[13]), .reset(rst));  // open: Qn, preset, en
  D_Flip_Flop d_ff_15 (.clk(and_1_out), .D(dataIn[14]), .Q(dataOut[14]), .reset(rst));  // open: Qn, preset, en
  D_Flip_Flop d_ff_16 (.clk(and_1_out), .D(dataIn[15]), .Q(dataOut[15]), .reset(rst));  // open: Qn, preset, en
endmodule

module RegisterFile (
  input  WE,
  input  clk,
  input  rst,
  input  [15:0] RDVAL,
  input  [2:0] RD,
  input  [2:0] RS2,
  input  [2:0] RS1,
  output [15:0] RS2VAL,
  output [15:0] RS1VAL
);

  wire and_1_out, decoder_1_out0, decoder_1_out1, decoder_1_out2, decoder_1_out3, decoder_1_out4,
       decoder_1_out5, decoder_1_out6, decoder_1_out7;
  wire [15:0] r0_dataout, r1_dataout, r2_dataout, r3_dataout, r4_dataout, r5_dataout, r6_dataout, r7_dataout;

  Decoder decoder_1 (
    .DecoderInput(RD), .out0(decoder_1_out0), .out1(decoder_1_out1), .out2(decoder_1_out2),
    .out3(decoder_1_out3), .out4(decoder_1_out4), .out5(decoder_1_out5), .out6(decoder_1_out6),
    .out7(decoder_1_out7));
  and and_1 (and_1_out, clk, WE);
  _16bitRegister r0 (.dataIn(RDVAL), .clk(and_1_out), .we(decoder_1_out0), .rst(rst), .dataOut(r0_dataout));
  _16bitRegister r1 (.dataIn(RDVAL), .clk(and_1_out), .we(decoder_1_out1), .rst(rst), .dataOut(r1_dataout));
  _16bitRegister r2 (.dataIn(RDVAL), .clk(and_1_out), .we(decoder_1_out2), .rst(rst), .dataOut(r2_dataout));
  _16bitRegister r3 (.dataIn(RDVAL), .clk(and_1_out), .we(decoder_1_out3), .rst(rst), .dataOut(r3_dataout));
  _16bitRegister r4 (.dataIn(RDVAL), .clk(and_1_out), .we(decoder_1_out4), .rst(rst), .dataOut(r4_dataout));
  _16bitRegister r5 (.dataIn(RDVAL), .clk(and_1_out), .we(decoder_1_out5), .rst(rst), .dataOut(r5_dataout));
  _16bitRegister r6 (.dataIn(RDVAL), .clk(and_1_out), .we(decoder_1_out6), .rst(rst), .dataOut(r6_dataout));
  _16bitRegister r7 (.dataIn(RDVAL), .clk(and_1_out), .we(decoder_1_out7), .rst(rst), .dataOut(r7_dataout));
  Multiplexer #(.select(3), .width(16)) multiplexer_1 (
    .in0(r0_dataout), .in1(r1_dataout), .in2(r2_dataout), .in3(r3_dataout), .in4(r4_dataout),
    .in5(r5_dataout), .in6(r6_dataout), .in7(r7_dataout), .out(RS2VAL), .sel(RS2));  // open: en
  Multiplexer #(.select(3), .width(16)) multiplexer_2 (
    .in0(r0_dataout), .in1(r1_dataout), .in2(r2_dataout), .in3(r3_dataout), .in4(r4_dataout),
    .in5(r5_dataout), .in6(r6_dataout), .in7(r7_dataout), .out(RS1VAL), .sel(RS1));  // open: en
endmodule

module Decoder (
  input  [2:0] DecoderInput,
  output out0,
  output out1,
  output out2,
  output out3,
  output out4,
  output out5,
  output out6,
  output out7
);

  wire not_1_out, not_2_out, not_3_out;

  not not_1 (not_1_out, DecoderInput[0]);
  not not_2 (not_2_out, DecoderInput[1]);
  not not_3 (not_3_out, DecoderInput[2]);
  and and_1 (out0, not_1_out, not_2_out, not_3_out);
  and and_2 (out1, DecoderInput[0], not_2_out, not_3_out);
  and and_3 (out2, not_1_out, DecoderInput[1], not_3_out);
  and and_4 (out3, DecoderInput[0], DecoderInput[1], not_3_out);
  and and_5 (out4, not_1_out, not_2_out, DecoderInput[2]);
  and and_6 (out5, DecoderInput[0], not_2_out, DecoderInput[2]);
  and and_7 (out6, not_1_out, DecoderInput[1], DecoderInput[2]);
  and and_8 (out7, DecoderInput[0], DecoderInput[1], DecoderInput[2]);
endmodule

module Adder (
  input  sub,
  input  [15:0] numA,
  input  [15:0] numB,
  output [15:0] Result,
  output ovf
);

  wire and_1_out, and_2_out, and_3_out, and_4_out, and_5_out, and_6_out, and_7_out, and_8_out, and_9_out,
       and_10_out, and_11_out, and_12_out, and_13_out, and_14_out, and_15_out, and_16_out, and_17_out,
       and_18_out, and_19_out, and_20_out, and_21_out, and_22_out, and_23_out, and_24_out, and_25_out,
       and_26_out, and_27_out, and_28_out, and_29_out, and_30_out, and_31_out, and_32_out, or_1_out,
       or_2_out, or_3_out, or_4_out, or_5_out, or_6_out, or_7_out, or_8_out, or_9_out, or_10_out, or_11_out,
       or_12_out, or_13_out, or_14_out, or_15_out, or_16_out, xor_3_out, xor_4_out, xor_6_out, xor_7_out,
       xor_9_out, xor_10_out, xor_11_out, xor_13_out, xor_15_out, xor_16_out, xor_18_out, xor_19_out,
       xor_21_out, xor_22_out, xor_23_out, xor_25_out, xor_27_out, xor_28_out, xor_30_out, xor_31_out,
       xor_33_out, xor_34_out, xor_35_out, xor_37_out, xor_39_out, xor_40_out, xor_42_out, xor_43_out,
       xor_45_out, xor_46_out, xor_47_out, xor_49_out;

  xor xor_1 (ovf, or_2_out, or_1_out);
  or or_1 (or_1_out, and_1_out, and_2_out);
  and and_1 (and_1_out, xor_3_out, or_2_out);
  and and_2 (and_2_out, numA[15], xor_4_out);
  xor xor_2 (Result[15], xor_3_out, or_2_out);
  xor xor_3 (xor_3_out, numA[15], xor_4_out);
  xor xor_4 (xor_4_out, sub, numB[15]);
  or or_2 (or_2_out, and_3_out, and_4_out);
  and and_3 (and_3_out, xor_6_out, or_3_out);
  and and_4 (and_4_out, numA[14], xor_7_out);
  xor xor_5 (Result[14], xor_6_out, or_3_out);
  xor xor_6 (xor_6_out, numA[14], xor_7_out);
  xor xor_7 (xor_7_out, sub, numB[14]);
  or or_3 (or_3_out, and_5_out, and_6_out);
  and and_5 (and_5_out, xor_9_out, or_4_out);
  and and_6 (and_6_out, numA[13], xor_10_out);
  xor xor_8 (Result[13], xor_9_out, or_4_out);
  xor xor_9 (xor_9_out, numA[13], xor_10_out);
  xor xor_10 (xor_10_out, sub, numB[13]);
  or or_4 (or_4_out, and_7_out, and_8_out);
  and and_7 (and_7_out, xor_11_out, or_5_out);
  and and_8 (and_8_out, numA[12], xor_13_out);
  xor xor_11 (xor_11_out, numA[12], xor_13_out);
  xor xor_12 (Result[12], xor_11_out, or_5_out);
  xor xor_13 (xor_13_out, sub, numB[12]);
  or or_5 (or_5_out, and_9_out, and_10_out);
  and and_9 (and_9_out, xor_15_out, or_6_out);
  and and_10 (and_10_out, numA[11], xor_16_out);
  xor xor_14 (Result[11], xor_15_out, or_6_out);
  xor xor_15 (xor_15_out, numA[11], xor_16_out);
  xor xor_16 (xor_16_out, sub, numB[11]);
  or or_6 (or_6_out, and_11_out, and_12_out);
  and and_11 (and_11_out, xor_18_out, or_7_out);
  and and_12 (and_12_out, numA[10], xor_19_out);
  xor xor_17 (Result[10], xor_18_out, or_7_out);
  xor xor_18 (xor_18_out, numA[10], xor_19_out);
  xor xor_19 (xor_19_out, sub, numB[10]);
  or or_7 (or_7_out, and_13_out, and_14_out);
  and and_13 (and_13_out, xor_21_out, or_8_out);
  and and_14 (and_14_out, numA[9], xor_22_out);
  xor xor_20 (Result[9], xor_21_out, or_8_out);
  xor xor_21 (xor_21_out, numA[9], xor_22_out);
  xor xor_22 (xor_22_out, sub, numB[9]);
  or or_8 (or_8_out, and_15_out, and_16_out);
  and and_15 (and_15_out, xor_23_out, or_9_out);
  and and_16 (and_16_out, numA[8], xor_25_out);
  xor xor_23 (xor_23_out, numA[8], xor_25_out);
  xor xor_24 (Result[8], xor_23_out, or_9_out);
  xor xor_25 (xor_25_out, sub, numB[8]);
  or or_9 (or_9_out, and_17_out, and_18_out);
  and and_17 (and_17_out, xor_27_out, or_10_out);
  and and_18 (and_18_out, numA[7], xor_28_out);
  xor xor_26 (Result[7], xor_27_out, or_10_out);
  xor xor_27 (xor_27_out, numA[7], xor_28_out);
  xor xor_28 (xor_28_out, sub, numB[7]);
  or or_10 (or_10_out, and_19_out, and_20_out);
  and and_19 (and_19_out, xor_30_out, or_11_out);
  and and_20 (and_20_out, numA[6], xor_31_out);
  xor xor_29 (Result[6], xor_30_out, or_11_out);
  xor xor_30 (xor_30_out, numA[6], xor_31_out);
  xor xor_31 (xor_31_out, sub, numB[6]);
  or or_11 (or_11_out, and_21_out, and_22_out);
  and and_21 (and_21_out, xor_33_out, or_12_out);
  and and_22 (and_22_out, numA[5], xor_34_out);
  xor xor_32 (Result[5], xor_33_out, or_12_out);
  xor xor_33 (xor_33_out, numA[5], xor_34_out);
  xor xor_34 (xor_34_out, sub, numB[5]);
  or or_12 (or_12_out, and_23_out, and_24_out);
  and and_23 (and_23_out, xor_35_out, or_13_out);
  and and_24 (and_24_out, numA[4], xor_37_out);
  xor xor_35 (xor_35_out, numA[4], xor_37_out);
  xor xor_36 (Result[4], xor_35_out, or_13_out);
  xor xor_37 (xor_37_out, sub, numB[4]);
  or or_13 (or_13_out, and_25_out, and_26_out);
  and and_25 (and_25_out, xor_39_out, or_14_out);
  and and_26 (and_26_out, numA[3], xor_40_out);
  xor xor_38 (Result[3], xor_39_out, or_14_out);
  xor xor_39 (xor_39_out, numA[3], xor_40_out);
  xor xor_40 (xor_40_out, sub, numB[3]);
  or or_14 (or_14_out, and_27_out, and_28_out);
  and and_27 (and_27_out, xor_42_out, or_15_out);
  and and_28 (and_28_out, numA[2], xor_43_out);
  xor xor_41 (Result[2], xor_42_out, or_15_out);
  xor xor_42 (xor_42_out, numA[2], xor_43_out);
  xor xor_43 (xor_43_out, sub, numB[2]);
  or or_15 (or_15_out, and_29_out, and_30_out);
  and and_29 (and_29_out, xor_45_out, or_16_out);
  and and_30 (and_30_out, numA[1], xor_46_out);
  xor xor_44 (Result[1], xor_45_out, or_16_out);
  xor xor_45 (xor_45_out, numA[1], xor_46_out);
  xor xor_46 (xor_46_out, sub, numB[1]);
  or or_16 (or_16_out, and_31_out, and_32_out);
  and and_31 (and_31_out, xor_47_out, sub);
  and and_32 (and_32_out, numA[0], xor_49_out);
  xor xor_47 (xor_47_out, numA[0], xor_49_out);
  xor xor_48 (Result[0], xor_47_out, sub);
  xor xor_49 (xor_49_out, sub, numB[0]);

  // Other names for the same wires on the sheet: b0 = numB[0]; b1 = numB[1]; b2 = numB[2]; b3 = numB[3]; b4 = numB[4];
  //   b5 = numB[5]; b6 = numB[6]; b7 = numB[7]; b8 = numB[8]; b9 = numB[9]; b10 = numB[10]; b11 = numB[11];
  //   b12 = numB[12]; b13 = numB[13]; b14 = numB[14]; b15 = numB[15]
endmodule

module ALU (
  input  [15:0] numA,
  input  [15:0] numB,
  input  [2:0] ALUop,
  input  [2:0] shamt,
  output [15:0] Result
);

  wire ADD, NAND, not_1_out, not_2_out, not_3_out, SHL, SHRA, SUB, XOR;
  wire [15:0] ADDResult, NANDResult, SHLResult, SHRAResult, undriven, undriven_2, XORResult;

  not not_1 (not_1_out, ALUop[0]);
  not not_2 (not_2_out, ALUop[2]);
  not not_3 (not_3_out, ALUop[1]);
  and and_1 (NAND, not_1_out, ALUop[1], not_2_out);
  and and_2 (XOR, ALUop[0], ALUop[1], not_2_out);
  and and_3 (ADD, not_1_out, not_3_out, not_2_out);
  and and_4 (SUB, ALUop[0], not_3_out, not_2_out);
  and and_5 (SHRA, not_1_out, not_3_out, ALUop[2]);
  and and_6 (SHL, ALUop[0], not_3_out, ALUop[2]);
  Adder Adder (.sub(SUB), .Result(ADDResult), .numA(numA), .numB(numB));  // open: ovf
  assign XORResult = numA ^ numB;  // XOR_Gate xor_1, 16 bits wide
  assign NANDResult = ~(numA & numB);  // NAND_Gate nand_1, 16 bits wide
  // Probe on ADDResult
  // Probe on XORResult
  // Probe on NANDResult
  // Probe on SHRAResult
  ShiftRight shiftright_1 (.shamt(shamt), .DataIn(numA), .Shifted(SHRAResult));
  // Probe on SHLResult
  ShiftLeft shiftleft_1 (.shamt(shamt), .DataIn(numA), .Shifted(SHLResult));
  Multiplexer #(.select(3), .width(16)) multiplexer_1 (
    .in0(ADDResult), .in1(ADDResult), .in2(NANDResult), .in3(XORResult), .in4(SHRAResult), .in5(SHLResult),
    .in6(undriven), .in7(undriven_2), .out(Result), .sel(ALUop));  // open: en
endmodule

module Extender (
  input  [5:0] immediate,
  output [15:0] extended
);

  wire [9:0] not_1_out;

  assign not_1_out = ~{10{1'b1}};  // NOT_Gate not_1, 10 bits wide
  Multiplexer #(.width(10)) multiplexer_1 (
    .in0(not_1_out), .in1({10{1'b1}}), .out(extended[15:6]), .sel(immediate[5]));  // open: en

  assign extended[5:0] = immediate;
endmodule

module _1BitShiftRight (
  input  [15:0] In,
  output [15:0] _1BitRight
);

  Multiplexer multiplexer_1 (.in0(In[0]), .in1(In[1]), .out(_1BitRight[0]), .sel(1'b1));  // open: en
  Multiplexer multiplexer_2 (.in0(In[1]), .in1(In[2]), .out(_1BitRight[1]), .sel(1'b1));  // open: en
  Multiplexer multiplexer_3 (.in0(In[2]), .in1(In[3]), .out(_1BitRight[2]), .sel(1'b1));  // open: en
  Multiplexer multiplexer_4 (.in0(In[3]), .in1(In[4]), .out(_1BitRight[3]), .sel(1'b1));  // open: en
  Multiplexer multiplexer_5 (.in0(In[4]), .in1(In[5]), .out(_1BitRight[4]), .sel(1'b1));  // open: en
  Multiplexer multiplexer_6 (.in0(In[5]), .in1(In[6]), .out(_1BitRight[5]), .sel(1'b1));  // open: en
  Multiplexer multiplexer_7 (.in0(In[6]), .in1(In[7]), .out(_1BitRight[6]), .sel(1'b1));  // open: en
  Multiplexer multiplexer_8 (.in0(In[7]), .in1(In[8]), .out(_1BitRight[7]), .sel(1'b1));  // open: en
  Multiplexer multiplexer_9 (.in0(In[8]), .in1(In[9]), .out(_1BitRight[8]), .sel(1'b1));  // open: en
  Multiplexer multiplexer_10 (.in0(In[9]), .in1(In[10]), .out(_1BitRight[9]), .sel(1'b1));  // open: en
  Multiplexer multiplexer_11 (.in0(In[10]), .in1(In[11]), .out(_1BitRight[10]), .sel(1'b1));  // open: en
  Multiplexer multiplexer_12 (.in0(In[11]), .in1(In[12]), .out(_1BitRight[11]), .sel(1'b1));  // open: en
  Multiplexer multiplexer_13 (.in0(In[12]), .in1(In[13]), .out(_1BitRight[12]), .sel(1'b1));  // open: en
  Multiplexer multiplexer_14 (.in0(In[13]), .in1(In[14]), .out(_1BitRight[13]), .sel(1'b1));  // open: en
  Multiplexer multiplexer_15 (.in0(In[14]), .in1(In[15]), .out(_1BitRight[14]), .sel(1'b1));  // open: en
  Multiplexer multiplexer_16 (.in0(In[15]), .in1(1'b0), .out(_1BitRight[15]), .sel(1'b1));  // open: en
endmodule

module ShiftRight (
  input  [2:0] shamt,
  input  [15:0] DataIn,
  output [15:0] Shifted
);

  wire [15:0] n1bitshiftright_1__1bitright, n1bitshiftright_2__1bitright, n1bitshiftright_3__1bitright,
       n1bitshiftright_4__1bitright, n1bitshiftright_5__1bitright, n1bitshiftright_6__1bitright,
       n1bitshiftright_7__1bitright;

  _1BitShiftRight u_1bitshiftright_1 (.In(DataIn), ._1BitRight(n1bitshiftright_1__1bitright));
  _1BitShiftRight u_1bitshiftright_2 (.In(n1bitshiftright_1__1bitright), ._1BitRight(n1bitshiftright_2__1bitright));
  _1BitShiftRight u_1bitshiftright_3 (.In(n1bitshiftright_2__1bitright), ._1BitRight(n1bitshiftright_3__1bitright));
  Multiplexer #(.select(3), .width(16)) multiplexer_1 (
    .in0(DataIn), .in1(n1bitshiftright_1__1bitright), .in2(n1bitshiftright_2__1bitright),
    .in3(n1bitshiftright_3__1bitright), .in4(n1bitshiftright_5__1bitright),
    .in5(n1bitshiftright_4__1bitright), .in6(n1bitshiftright_6__1bitright),
    .in7(n1bitshiftright_7__1bitright), .out(Shifted), .sel(shamt));  // open: en
  _1BitShiftRight u_1bitshiftright_4 (.In(n1bitshiftright_5__1bitright), ._1BitRight(n1bitshiftright_4__1bitright));
  _1BitShiftRight u_1bitshiftright_5 (.In(n1bitshiftright_3__1bitright), ._1BitRight(n1bitshiftright_5__1bitright));
  _1BitShiftRight u_1bitshiftright_6 (.In(n1bitshiftright_4__1bitright), ._1BitRight(n1bitshiftright_6__1bitright));
  _1BitShiftRight u_1bitshiftright_7 (.In(n1bitshiftright_6__1bitright), ._1BitRight(n1bitshiftright_7__1bitright));
endmodule

module _1BitShiftLeft (
  input  [15:0] In,
  output [15:0] _1BitLeft
);

  Multiplexer multiplexer_1 (.in0(In[15]), .in1(In[14]), .out(_1BitLeft[15]), .sel(1'b1));  // open: en
  Multiplexer multiplexer_2 (.in0(In[14]), .in1(In[13]), .out(_1BitLeft[14]), .sel(1'b1));  // open: en
  Multiplexer multiplexer_3 (.in0(In[13]), .in1(In[12]), .out(_1BitLeft[13]), .sel(1'b1));  // open: en
  Multiplexer multiplexer_4 (.in0(In[12]), .in1(In[11]), .out(_1BitLeft[12]), .sel(1'b1));  // open: en
  Multiplexer multiplexer_5 (.in0(In[11]), .in1(In[10]), .out(_1BitLeft[11]), .sel(1'b1));  // open: en
  Multiplexer multiplexer_6 (.in0(In[10]), .in1(In[9]), .out(_1BitLeft[10]), .sel(1'b1));  // open: en
  Multiplexer multiplexer_7 (.in0(In[9]), .in1(In[8]), .out(_1BitLeft[9]), .sel(1'b1));  // open: en
  Multiplexer multiplexer_8 (.in0(In[8]), .in1(In[7]), .out(_1BitLeft[8]), .sel(1'b1));  // open: en
  Multiplexer multiplexer_9 (.in0(In[7]), .in1(In[6]), .out(_1BitLeft[7]), .sel(1'b1));  // open: en
  Multiplexer multiplexer_10 (.in0(In[6]), .in1(In[5]), .out(_1BitLeft[6]), .sel(1'b1));  // open: en
  Multiplexer multiplexer_11 (.in0(In[5]), .in1(In[4]), .out(_1BitLeft[5]), .sel(1'b1));  // open: en
  Multiplexer multiplexer_12 (.in0(In[4]), .in1(In[3]), .out(_1BitLeft[4]), .sel(1'b1));  // open: en
  Multiplexer multiplexer_13 (.in0(In[3]), .in1(In[2]), .out(_1BitLeft[3]), .sel(1'b1));  // open: en
  Multiplexer multiplexer_14 (.in0(In[2]), .in1(In[1]), .out(_1BitLeft[2]), .sel(1'b1));  // open: en
  Multiplexer multiplexer_15 (.in0(In[1]), .in1(In[0]), .out(_1BitLeft[1]), .sel(1'b1));  // open: en
  Multiplexer multiplexer_16 (.in0(In[0]), .in1(1'b0), .out(_1BitLeft[0]), .sel(1'b1));  // open: en
endmodule

module ShiftLeft (
  input  [2:0] shamt,
  input  [15:0] DataIn,
  output [15:0] Shifted
);

  wire [15:0] n1bitshiftleft_1__1bitleft, n1bitshiftleft_2__1bitleft, n1bitshiftleft_3__1bitleft,
       n1bitshiftleft_4__1bitleft, n1bitshiftleft_5__1bitleft, n1bitshiftleft_6__1bitleft,
       n1bitshiftleft_7__1bitleft;

  _1BitShiftLeft u_1bitshiftleft_1 (.In(DataIn), ._1BitLeft(n1bitshiftleft_1__1bitleft));
  _1BitShiftLeft u_1bitshiftleft_2 (.In(n1bitshiftleft_1__1bitleft), ._1BitLeft(n1bitshiftleft_2__1bitleft));
  _1BitShiftLeft u_1bitshiftleft_3 (.In(n1bitshiftleft_2__1bitleft), ._1BitLeft(n1bitshiftleft_3__1bitleft));
  Multiplexer #(.select(3), .width(16)) multiplexer_1 (
    .in0(DataIn), .in1(n1bitshiftleft_1__1bitleft), .in2(n1bitshiftleft_2__1bitleft),
    .in3(n1bitshiftleft_3__1bitleft), .in4(n1bitshiftleft_4__1bitleft), .in5(n1bitshiftleft_5__1bitleft),
    .in6(n1bitshiftleft_6__1bitleft), .in7(n1bitshiftleft_7__1bitleft), .out(Shifted), .sel(shamt));  // open: en
  _1BitShiftLeft u_1bitshiftleft_4 (.In(n1bitshiftleft_3__1bitleft), ._1BitLeft(n1bitshiftleft_4__1bitleft));
  _1BitShiftLeft u_1bitshiftleft_5 (.In(n1bitshiftleft_4__1bitleft), ._1BitLeft(n1bitshiftleft_5__1bitleft));
  _1BitShiftLeft u_1bitshiftleft_6 (.In(n1bitshiftleft_5__1bitleft), ._1BitLeft(n1bitshiftleft_6__1bitleft));
  _1BitShiftLeft u_1bitshiftleft_7 (.In(n1bitshiftleft_6__1bitleft), ._1BitLeft(n1bitshiftleft_7__1bitleft));
endmodule

module PCIncrement (
  input  [15:0] PCIn,
  output [15:0] PCOut
);

  Adder adder_1 (.sub(1'b0), .Result(PCOut), .numA(PCIn), .numB(16'h1));  // open: ovf
endmodule
