// Logisim project hw4CorrectRegisterFile Passes Five Tests.circ as structural Verilog: 21 circuits, main circuit main
module main (
  input  reset
);

  wire ALUinB, and_1_out, and_2_out, and_3_out, and_4_out, Beqz, Bgt, Br, BrMet, clock_1_out, DMwe, Input,
       InputAvailable, isEqualZero_allzero, isGreater_greater, Jal, Jp, Jr, not_1_out, not_2_out, or_1_out,
       Output, Rdst, Rwd, WE;
  wire [2:0] ALUop, multiplexer_2_out, multiplexer_3_out, rd, rs, rt, shamt;
  wire [3:0] instructiondecoder_1_opcode;
  wire [5:0] immed;
  wire [6:0] keyboard_1_data, lower7bits_1_ascii, multiplexer_9_out;
  wire [11:0] _12BitAddress;
  wire [15:0] ALU_result, CurrentPC, immediate, jumpaddress_1_pcout, KeyboardInput, multiplexer_4_out,
       multiplexer_5_out, multiplexer_6_out, multiplexer_7_out, multiplexer_8_out, multiplexer_10_out,
       NextPC, PCIncremented, PCPlusImmePlus1_pcout, ram_1_data, RegisterFile_rs1val, rom_1_data, rsData;

  PCRegister pcregister_1 (.dataIn(NextPC), .clk(clock_1_out), .rst(reset), .dataOut(CurrentPC));
  ROM #(.addrWidth(16), .dataWidth(16)) rom_1 (.addr(CurrentPC), .data(rom_1_data));  // open: sel
  Clock clock_1 (.out(clock_1_out));
  not not_1 (not_1_out, clock_1_out);
  Multiplexer #(.width(16)) multiplexer_1 (.in0(multiplexer_4_out), .in1(rsData), .out(NextPC), .sel(Jr));  // open: en
  Multiplexer #(.width(3)) multiplexer_2 (
    .in0(multiplexer_3_out), .in1(3'b111), .out(multiplexer_2_out), .sel(Jal));  // open: en
  Multiplexer #(.width(3)) multiplexer_3 (.in0(rd), .in1(rt), .out(multiplexer_3_out), .sel(Rdst));  // open: en
  Multiplexer #(.width(16)) multiplexer_4 (
    .in0(multiplexer_5_out), .in1(jumpaddress_1_pcout), .out(multiplexer_4_out), .sel(or_1_out));  // open: en
  or or_1 (or_1_out, Jal, Jp);
  regfile RegisterFile (
    .clk(clock_1_out), .rst(reset), .RDVAL(multiplexer_7_out), .RD(multiplexer_2_out), .WE(WE), .RS2(rs),
    .RS1(rt), .RS2VAL(rsData), .RS1VAL(RegisterFile_rs1val));
  Multiplexer #(.width(16)) multiplexer_5 (
    .in0(PCIncremented), .in1(PCPlusImmePlus1_pcout), .out(multiplexer_5_out), .sel(and_1_out));  // open: en
  JumpAddress jumpaddress_1 (._12BitAddress(_12BitAddress), .PCIn(CurrentPC), .PCOut(jumpaddress_1_pcout));
  PCIncrement PCPlus1 (.PCOut(PCIncremented), .PCIn(CurrentPC));
  BranchPC PCPlusImmePlus1 (.PCIn(CurrentPC), .Immediate(immediate), .PCOut(PCPlusImmePlus1_pcout));
  and and_1 (and_1_out, Br, BrMet);
  Multiplexer #(.width(16)) multiplexer_6 (
    .in0(multiplexer_10_out), .in1(PCIncremented), .out(multiplexer_6_out), .sel(Jal));  // open: en
  Multiplexer #(.width(16)) multiplexer_7 (
    .in0(multiplexer_6_out), .in1(KeyboardInput), .out(multiplexer_7_out), .sel(Input));  // open: en
  InstructionDecoder instructiondecoder_1 (
    .Instruction(rom_1_data), .shamt(shamt), .rd(rd), .rt(rt), .rs(rs), .opcode(instructiondecoder_1_opcode),
    .immediate(immed), .address(_12BitAddress));
  Extender BitExtender (.extended(immediate), .immediate(immed));
  Multiplexer #(.width(16)) multiplexer_8 (
    .in0(RegisterFile_rs1val), .in1(immediate), .out(multiplexer_8_out), .sel(ALUinB));  // open: en
  OpcodeDecoder opcodedecoder_1 (
    .opcode(instructiondecoder_1_opcode), .Input(Input), .WE(WE), .Output(Output), .Rdst(Rdst), .DMwe(DMwe),
    .Rwd(Rwd), .ALUinB(ALUinB), .Br(Br), .Jp(Jp), .ALUop(ALUop), .Jr(Jr), .Beqz(Beqz), .Jal(Jal), .Bgt(Bgt));
  EqualZero isEqualZero (.NumIn(rsData), .AllZero(isEqualZero_allzero));
  Greater isGreater (.SUBRes(ALU_result), .Greater(isGreater_greater));
  ALU ALU (.numA(rsData), .numB(multiplexer_8_out), .ALUop(ALUop), .shamt(shamt), .Result(ALU_result));
  Lower7Bits lower7bits_1 (.DataToPrint(rsData), .ASCII(lower7bits_1_ascii));
  and and_2 (and_2_out, Beqz, isEqualZero_allzero);
  and and_3 (and_3_out, isGreater_greater, Bgt);
  not not_2 (not_2_out, DMwe);
  Multiplexer #(.width(7)) multiplexer_9 (
    .in0({7{1'b0}}), .in1(lower7bits_1_ascii), .out(multiplexer_9_out), .sel(Output));  // open: en
  or or_2 (BrMet, and_2_out, and_3_out);
  RAM #(.addrWidth(16), .dataWidth(16), .bus("separate")) ram_1 (
    .addr(ALU_result), .din(RegisterFile_rs1val), .data(ram_1_data), .str(DMwe), .clk(not_1_out),
    .ld(not_2_out));  // open: sel, clr
  Multiplexer #(.width(16)) multiplexer_10 (
    .in0(ALU_result), .in1(ram_1_data), .out(multiplexer_10_out), .sel(Rwd));  // open: en
  TTY #(.rows(13), .cols(80)) tty_1 (.data(multiplexer_9_out), .clk(clock_1_out), .clr(reset));  // open: we
  Keyboard #(.trigger("falling")) keyboard_1 (
    .clk(and_4_out), .clr(reset), .avail(InputAvailable), .data(keyboard_1_data));  // open: re
  and and_4 (and_4_out, clock_1_out, Input);
  KeyboardInput keyboardinput_1 (.Keyboard(keyboard_1_data), .available(InputAvailable), .out_3(KeyboardInput));

  // Other names for the same wires on the sheet: GlobalReset = reset

  // Notes on the sheet:
  //   contents of rom_1 (hex, n*v repeats v):
  //   2100 2903 f008 22a0 e400 293f 8801 b002 803f
endmodule

module _16bitRegister (
  input  clk,
  input  we,
  input  rst,
  input  [15:0] dataIn,
  output [15:0] dataOut
);

  wire and_1_out;

  and and_1 (and_1_out, clk, we);
  D_Flip_Flop #(.trigger("falling")) d_ff_1 (
    .clk(and_1_out), .D(dataIn[0]), .Q(dataOut[0]), .reset(rst));  // open: Qn, preset, en
  D_Flip_Flop #(.trigger("falling")) d_ff_2 (
    .clk(and_1_out), .D(dataIn[1]), .Q(dataOut[1]), .reset(rst));  // open: Qn, preset, en
  D_Flip_Flop #(.trigger("falling")) d_ff_3 (
    .clk(and_1_out), .D(dataIn[2]), .Q(dataOut[2]), .reset(rst));  // open: Qn, preset, en
  D_Flip_Flop #(.trigger("falling")) d_ff_4 (
    .clk(and_1_out), .D(dataIn[3]), .Q(dataOut[3]), .reset(rst));  // open: Qn, preset, en
  D_Flip_Flop #(.trigger("falling")) d_ff_5 (
    .clk(and_1_out), .D(dataIn[4]), .Q(dataOut[4]), .reset(rst));  // open: Qn, preset, en
  D_Flip_Flop #(.trigger("falling")) d_ff_6 (
    .clk(and_1_out), .D(dataIn[5]), .Q(dataOut[5]), .reset(rst));  // open: Qn, preset, en
  D_Flip_Flop #(.trigger("falling")) d_ff_7 (
    .clk(and_1_out), .D(dataIn[6]), .Q(dataOut[6]), .reset(rst));  // open: Qn, preset, en
  D_Flip_Flop #(.trigger("falling")) d_ff_8 (
    .clk(and_1_out), .D(dataIn[7]), .Q(dataOut[7]), .reset(rst));  // open: Qn, preset, en
  D_Flip_Flop #(.trigger("falling")) d_ff_9 (
    .clk(and_1_out), .D(dataIn[8]), .Q(dataOut[8]), .reset(rst));  // open: Qn, preset, en
  D_Flip_Flop #(.trigger("falling")) d_ff_10 (
    .clk(and_1_out), .D(dataIn[9]), .Q(dataOut[9]), .reset(rst));  // open: Qn, preset, en
  D_Flip_Flop #(.trigger("falling")) d_ff_11 (
    .clk(and_1_out), .D(dataIn[10]), .Q(dataOut[10]), .reset(rst));  // open: Qn, preset, en
  D_Flip_Flop #(.trigger("falling")) d_ff_12 (
    .clk(and_1_out), .D(dataIn[11]), .Q(dataOut[11]), .reset(rst));  // open: Qn, preset, en
  D_Flip_Flop #(.trigger("falling")) d_ff_13 (
    .clk(and_1_out), .D(dataIn[12]), .Q(dataOut[12]), .reset(rst));  // open: Qn, preset, en
  D_Flip_Flop #(.trigger("falling")) d_ff_14 (
    .clk(and_1_out), .D(dataIn[13]), .Q(dataOut[13]), .reset(rst));  // open: Qn, preset, en
  D_Flip_Flop #(.trigger("falling")) d_ff_15 (
    .clk(and_1_out), .D(dataIn[14]), .Q(dataOut[14]), .reset(rst));  // open: Qn, preset, en
  D_Flip_Flop #(.trigger("falling")) d_ff_16 (
    .clk(and_1_out), .D(dataIn[15]), .Q(dataOut[15]), .reset(rst));  // open: Qn, preset, en
endmodule

module regfile (
  input  clk,
  input  WE,
  input  rst,
  input  [15:0] RDVAL,
  input  [2:0] RD,
  input  [2:0] RS2,
  input  [2:0] RS1,
  output [15:0] RS2VAL,
  output [15:0] RS1VAL
);

  wire and_1_out, and_2_out, and_3_out, and_4_out, and_5_out, and_6_out, and_7_out, and_8_out,
       decoder_1_out0, decoder_1_out1, decoder_1_out2, decoder_1_out3, decoder_1_out4, decoder_1_out5,
       decoder_1_out6, decoder_1_out7;
  wire [15:0] r0_dataout, r1_dataout, r2_dataout, r3_dataout, r4_dataout, r5_dataout, r6_dataout, r7_dataout;

  Decoder decoder_1 (
    .DecoderInput(RD), .out0(decoder_1_out0), .out1(decoder_1_out1), .out2(decoder_1_out2),
    .out3(decoder_1_out3), .out4(decoder_1_out4), .out5(decoder_1_out5), .out6(decoder_1_out6),
    .out7(decoder_1_out7));
  and and_1 (and_1_out, decoder_1_out0, WE);
  and and_2 (and_2_out, decoder_1_out1, WE);
  and and_3 (and_3_out, decoder_1_out2, WE);
  and and_4 (and_4_out, decoder_1_out3, WE);
  and and_5 (and_5_out, decoder_1_out4, WE);
  and and_6 (and_6_out, decoder_1_out5, WE);
  and and_7 (and_7_out, decoder_1_out6, WE);
  and and_8 (and_8_out, decoder_1_out7, WE);
  _16bitRegister r0 (.dataIn(RDVAL), .clk(clk), .we(and_1_out), .rst(rst), .dataOut(r0_dataout));
  _16bitRegister r1 (.dataIn(RDVAL), .clk(clk), .we(and_2_out), .rst(rst), .dataOut(r1_dataout));
  _16bitRegister r2 (.dataIn(RDVAL), .clk(clk), .we(and_3_out), .rst(rst), .dataOut(r2_dataout));
  _16bitRegister r3 (.dataIn(RDVAL), .clk(clk), .we(and_4_out), .rst(rst), .dataOut(r3_dataout));
  _16bitRegister r4 (.dataIn(RDVAL), .clk(clk), .we(and_5_out), .rst(rst), .dataOut(r4_dataout));
  _16bitRegister r5 (.dataIn(RDVAL), .clk(clk), .we(and_6_out), .rst(rst), .dataOut(r5_dataout));
  _16bitRegister r6 (.dataIn(RDVAL), .clk(clk), .we(and_7_out), .rst(rst), .dataOut(r6_dataout));
  _16bitRegister r7 (.dataIn(RDVAL), .clk(clk), .we(and_8_out), .rst(rst), .dataOut(r7_dataout));
  Multiplexer #(.select(3), .width(16)) multiplexer_1 (
    .in0(r0_dataout), .in1(r1_dataout), .in2(r2_dataout), .in3(r3_dataout), .in4(r4_dataout),
    .in5(r5_dataout), .in6(r6_dataout), .in7(r7_dataout), .out(RS2VAL), .sel(RS2));  // open: en
  Multiplexer #(.select(3), .width(16)) multiplexer_2 (
    .in0(r0_dataout), .in1(r1_dataout), .in2(r2_dataout), .in3(r3_dataout), .in4(r4_dataout),
    .in5(r5_dataout), .in6(r6_dataout), .in7(r7_dataout), .out(RS1VAL), .sel(RS1));  // open: en
  // Probe on r0_dataout
  // Probe on r1_dataout
  // Probe on r2_dataout
  // Probe on r3_dataout
  // Probe on r4_dataout
  // Probe on r5_dataout
  // Probe on r6_dataout
  // Probe on r7_dataout
endmodule

module Decoder (
  input  [2:0] DecoderInput,
  output out0,
  output out1,
  output out2,
  output out3,
  output out4,
  output out5,
  output out6,
  output out7
);

  wire not_1_out, not_2_out, not_3_out;

  not not_1 (not_1_out, DecoderInput[0]);
  not not_2 (not_2_out, DecoderInput[1]);
  not not_3 (not_3_out, DecoderInput[2]);
  and and_1 (out0, not_1_out, not_2_out, not_3_out);
  and and_2 (out1, DecoderInput[0], not_2_out, not_3_out);
  and and_3 (out2, not_1_out, DecoderInput[1], not_3_out);
  and and_4 (out3, DecoderInput[0], DecoderInput[1], not_3_out);
  and and_5 (out4, not_1_out, not_2_out, DecoderInput[2]);
  and and_6 (out5, DecoderInput[0], not_2_out, DecoderInput[2]);
  and and_7 (out6, not_1_out, DecoderInput[1], DecoderInput[2]);
  and and_8 (out7, DecoderInput[0], DecoderInput[1], DecoderInput[2]);
endmodule

module Adder (
  input  sub,
  input  [15:0] numA,
  input  [15:0] numB,
  output [15:0] Result,
  output ovf
);

  wire and_1_out, and_2_out, and_3_out, and_4_out, and_5_out, and_6_out, and_7_out, and_8_out, and_9_out,
       and_10_out, and_11_out, and_12_out, and_13_out, and_14_out, and_15_out, and_16_out, and_17_out,
       and_18_out, and_19_out, and_20_out, and_21_out, and_22_out, and_23_out, and_24_out, and_25_out,
       and_26_out, and_27_out, and_28_out, and_29_out, and_30_out, and_31_out, and_32_out, or_1_out,
       or_2_out, or_3_out, or_4_out, or_5_out, or_6_out, or_7_out, or_8_out, or_9_out, or_10_out, or_11_out,
       or_12_out, or_13_out, or_14_out, or_15_out, or_16_out, xor_3_out, xor_4_out, xor_6_out, xor_7_out,
       xor_9_out, xor_10_out, xor_11_out, xor_13_out, xor_15_out, xor_16_out, xor_18_out, xor_19_out,
       xor_21_out, xor_22_out, xor_23_out, xor_25_out, xor_27_out, xor_28_out, xor_30_out, xor_31_out,
       xor_33_out, xor_34_out, xor_35_out, xor_37_out, xor_39_out, xor_40_out, xor_42_out, xor_43_out,
       xor_45_out, xor_46_out, xor_47_out, xor_49_out;

  xor xor_1 (ovf, or_2_out, or_1_out);
  or or_1 (or_1_out, and_1_out, and_2_out);
  and and_1 (and_1_out, xor_3_out, or_2_out);
  and and_2 (and_2_out, numA[15], xor_4_out);
  xor xor_2 (Result[15], xor_3_out, or_2_out);
  xor xor_3 (xor_3_out, numA[15], xor_4_out);
  xor xor_4 (xor_4_out, sub, numB[15]);
  or or_2 (or_2_out, and_3_out, and_4_out);
  and and_3 (and_3_out, xor_6_out, or_3_out);
  and and_4 (and_4_out, numA[14], xor_7_out);
  xor xor_5 (Result[14], xor_6_out, or_3_out);
  xor xor_6 (xor_6_out, numA[14], xor_7_out);
  xor xor_7 (xor_7_out, sub, numB[14]);
  or or_3 (or_3_out, and_5_out, and_6_out);
  and and_5 (and_5_out, xor_9_out, or_4_out);
  and and_6 (and_6_out, numA[13], xor_10_out);
  xor xor_8 (Result[13], xor_9_out, or_4_out);
  xor xor_9 (xor_9_out, numA[13], xor_10_out);
  xor xor_10 (xor_10_out, sub, numB[13]);
  or or_4 (or_4_out, and_7_out, and_8_out);
  and and_7 (and_7_out, xor_11_out, or_5_out);
  and and_8 (and_8_out, numA[12], xor_13_out);
  xor xor_11 (xor_11_out, numA[12], xor_13_out);
  xor xor_12 (Result[12], xor_11_out, or_5_out);
  xor xor_13 (xor_13_out, sub, numB[12]);
  or or_5 (or_5_out, and_9_out, and_10_out);
  and and_9 (and_9_out, xor_15_out, or_6_out);
  and and_10 (and_10_out, numA[11], xor_16_out);
  xor xor_14 (Result[11], xor_15_out, or_6_out);
  xor xor_15 (xor_15_out, numA[11], xor_16_out);
  xor xor_16 (xor_16_out, sub, numB[11]);
  or or_6 (or_6_out, and_11_out, and_12_out);
  and and_11 (and_11_out, xor_18_out, or_7_out);
  and and_12 (and_12_out, numA[10], xor_19_out);
  xor xor_17 (Result[10], xor_18_out, or_7_out);
  xor xor_18 (xor_18_out, numA[10], xor_19_out);
  xor xor_19 (xor_19_out, sub, numB[10]);
  or or_7 (or_7_out, and_13_out, and_14_out);
  and and_13 (and_13_out, xor_21_out, or_8_out);
  and and_14 (and_14_out, numA[9], xor_22_out);
  xor xor_20 (Result[9], xor_21_out, or_8_out);
  xor xor_21 (xor_21_out, numA[9], xor_22_out);
  xor xor_22 (xor_22_out, sub, numB[9]);
  or or_8 (or_8_out, and_15_out, and_16_out);
  and and_15 (and_15_out, xor_23_out, or_9_out);
  and and_16 (and_16_out, numA[8], xor_25_out);
  xor xor_23 (xor_23_out, numA[8], xor_25_out);
  xor xor_24 (Result[8], xor_23_out, or_9_out);
  xor xor_25 (xor_25_out, sub, numB[8]);
  or or_9 (or_9_out, and_17_out, and_18_out);
  and and_17 (and_17_out, xor_27_out, or_10_out);
  and and_18 (and_18_out, numA[7], xor_28_out);
  xor xor_26 (Result[7], xor_27_out, or_10_out);
  xor xor_27 (xor_27_out, numA[7], xor_28_out);
  xor xor_28 (xor_28_out, sub, numB[7]);
  or or_10 (or_10_out, and_19_out, and_20_out);
  and and_19 (and_19_out, xor_30_out, or_11_out);
  and and_20 (and_20_out, numA[6], xor_31_out);
  xor xor_29 (Result[6], xor_30_out, or_11_out);
  xor xor_30 (xor_30_out, numA[6], xor_31_out);
  xor xor_31 (xor_31_out, sub, numB[6]);
  or or_11 (or_11_out, and_21_out, and_22_out);
  and and_21 (and_21_out, xor_33_out, or_12_out);
  and and_22 (and_22_out, numA[5], xor_34_out);
  xor xor_32 (Result[5], xor_33_out, or_12_out);
  xor xor_33 (xor_33_out, numA[5], xor_34_out);
  xor xor_34 (xor_34_out, sub, numB[5]);
  or or_12 (or_12_out, and_23_out, and_24_out);
  and and_23 (and_23_out, xor_35_out, or_13_out);
  and and_24 (and_24_out, numA[4], xor_37_out);
  xor xor_35 (xor_35_out, numA[4], xor_37_out);
  xor xor_36 (Result[4], xor_35_out, or_13_out);
  xor xor_37 (xor_37_out, sub, numB[4]);
  or or_13 (or_13_out, and_25_out, and_26_out);
  and and_25 (and_25_out, xor_39_out, or_14_out);
  and and_26 (and_26_out, numA[3], xor_40_out);
  xor xor_38 (Result[3], xor_39_out, or_14_out);
  xor xor_39 (xor_39_out, numA[3], xor_40_out);
  xor xor_40 (xor_40_out, sub, numB[3]);
  or or_14 (or_14_out, and_27_out, and_28_out);
  and and_27 (and_27_out, xor_42_out, or_15_out);
  and and_28 (and_28_out, numA[2], xor_43_out);
  xor xor_41 (Result[2], xor_42_out, or_15_out);
  xor xor_42 (xor_42_out, numA[2], xor_43_out);
  xor xor_43 (xor_43_out, sub, numB[2]);
  or or_15 (or_15_out, and_29_out, and_30_out);
  and and_29 (and_29_out, xor_45_out, or_16_out);
  and and_30 (and_30_out, numA[1], xor_46_out);
  xor xor_44 (Result[1], xor_45_out, or_16_out);
  xor xor_45 (xor_45_out, numA[1], xor_46_out);
  xor xor_46 (xor_46_out, sub, numB[1]);
  or or_16 (or_16_out, and_31_out, and_32_out);
  and and_31 (and_31_out, xor_47_out, sub);
  and and_32 (and_32_out, numA[0], xor_49_out);
  xor xor_47 (xor_47_out, numA[0], xor_49_out);
  xor xor_48 (Result[0], xor_47_out, sub);
  xor xor_49 (xor_49_out, sub, numB[0]);

  // Other names for the same wires on the sheet: b0 = numB[0]; b1 = numB[1]; b2 = numB[2]; b3 = numB[3]; b4 = numB[4];
  //   b5 = numB[5]; b6 = numB[6]; b7 = numB[7]; b8 = numB[8]; b9 = numB[9]; b10 = numB[10]; b11 = numB[11];
  //   b12 = numB[12]; b13 = numB[13]; b14 = numB[14]; b15 = numB[15]
endmodule

module ALU (
  input  [15:0] numA,
  input  [15:0] numB,
  input  [2:0] ALUop,
  input  [2:0] shamt,
  output [15:0] Result
);

  wire ADD, NAND, not_1_out, not_2_out, not_3_out, SHL, SHRA, SUB, XOR;
  wire [15:0] ADDResult, NANDResult, SHLResult, SHRAResult, undriven, undriven_2, XORResult;

  not not_1 (not_1_out, ALUop[0]);
  not not_2 (not_2_out, ALUop[2]);
  not not_3 (not_3_out, ALUop[1]);
  and and_1 (NAND, not_1_out, ALUop[1], not_2_out);
  and and_2 (XOR, ALUop[0], ALUop[1], not_2_out);
  and and_3 (ADD, not_1_out, not_3_out, not_2_out);
  and and_4 (SUB, ALUop[0], not_3_out, not_2_out);
  and and_5 (SHRA, not_1_out, not_3_out, ALUop[2]);
  and and_6 (SHL, ALUop[0], not_3_out, ALUop[2]);
  Adder Adder (.sub(SUB), .Result(ADDResult), .numA(numA), .numB(numB));  // open: ovf
  assign XORResult = numA ^ numB;  // XOR_Gate xor_1, 16 bits wide
  assign NANDResult = ~(numA & numB);  // NAND_Gate nand_1, 16 bits wide
  ShiftRight shiftright_1 (.shamt(shamt), .DataIn(numA), .Shifted(SHRAResult));
  ShiftLeft shiftleft_1 (.shamt(shamt), .DataIn(numA), .Shifted(SHLResult));
  Multiplexer #(.select(3), .width(16)) multiplexer_1 (
    .in0(ADDResult), .in1(ADDResult), .in2(NANDResult), .in3(XORResult), .in4(SHRAResult), .in5(SHLResult),
    .in6(undriven), .in7(undriven_2), .out(Result), .sel(ALUop));  // open: en
endmodule

module Extender (
  input  [5:0] immediate,
  output [15:0] extended
);

  wire [9:0] not_1_out;

  assign not_1_out = ~{10{1'b1}};  // NOT_Gate not_1, 10 bits wide
  Multiplexer #(.width(10)) multiplexer_1 (
    .in0(not_1_out), .in1({10{1'b1}}), .out(extended[15:6]), .sel(immediate[5]));  // open: en

  assign extended[5:0] = immediate;
endmodule

module _1BitShiftRight (
  input  [15:0] In,
  output [15:0] _1BitRight
);

  Multiplexer multiplexer_1 (.in0(In[0]), .in1(In[1]), .out(_1BitRight[0]), .sel(1'b1));  // open: en
  Multiplexer multiplexer_2 (.in0(In[1]), .in1(In[2]), .out(_1BitRight[1]), .sel(1'b1));  // open: en
  Multiplexer multiplexer_3 (.in0(In[2]), .in1(In[3]), .out(_1BitRight[2]), .sel(1'b1));  // open: en
  Multiplexer multiplexer_4 (.in0(In[3]), .in1(In[4]), .out(_1BitRight[3]), .sel(1'b1));  // open: en
  Multiplexer multiplexer_5 (.in0(In[4]), .in1(In[5]), .out(_1BitRight[4]), .sel(1'b1));  // open: en
  Multiplexer multiplexer_6 (.in0(In[5]), .in1(In[6]), .out(_1BitRight[5]), .sel(1'b1));  // open: en
  Multiplexer multiplexer_7 (.in0(In[6]), .in1(In[7]), .out(_1BitRight[6]), .sel(1'b1));  // open: en
  Multiplexer multiplexer_8 (.in0(In[7]), .in1(In[8]), .out(_1BitRight[7]), .sel(1'b1));  // open: en
  Multiplexer multiplexer_9 (.in0(In[8]), .in1(In[9]), .out(_1BitRight[8]), .sel(1'b1));  // open: en
  Multiplexer multiplexer_10 (.in0(In[9]), .in1(In[10]), .out(_1BitRight[9]), .sel(1'b1));  // open: en
  Multiplexer multiplexer_11 (.in0(In[10]), .in1(In[11]), .out(_1BitRight[10]), .sel(1'b1));  // open: en
  Multiplexer multiplexer_12 (.in0(In[11]), .in1(In[12]), .out(_1BitRight[11]), .sel(1'b1));  // open: en
  Multiplexer multiplexer_13 (.in0(In[12]), .in1(In[13]), .out(_1BitRight[12]), .sel(1'b1));  // open: en
  Multiplexer multiplexer_14 (.in0(In[13]), .in1(In[14]), .out(_1BitRight[13]), .sel(1'b1));  // open: en
  Multiplexer multiplexer_15 (.in0(In[14]), .in1(In[15]), .out(_1BitRight[14]), .sel(1'b1));  // open: en
  Multiplexer multiplexer_16 (.in0(In[15]), .in1(1'b0), .out(_1BitRight[15]), .sel(1'b1));  // open: en
endmodule

module ShiftRight (
  input  [2:0] shamt,
  input  [15:0] DataIn,
  output [15:0] Shifted
);

  wire [15:0] n1bitshiftright_1__1bitright, n1bitshiftright_2__1bitright, n1bitshiftright_3__1bitright,
       n1bitshiftright_4__1bitright, n1bitshiftright_5__1bitright, n1bitshiftright_6__1bitright,
       n1bitshiftright_7__1bitright;

  _1BitShiftRight u_1bitshiftright_1 (.In(DataIn), ._1BitRight(n1bitshiftright_1__1bitright));
  _1BitShiftRight u_1bitshiftright_2 (.In(n1bitshiftright_1__1bitright), ._1BitRight(n1bitshiftright_2__1bitright));
  _1BitShiftRight u_1bitshiftright_3 (.In(n1bitshiftright_2__1bitright), ._1BitRight(n1bitshiftright_3__1bitright));
  Multiplexer #(.select(3), .width(16)) multiplexer_1 (
    .in0(DataIn), .in1(n1bitshiftright_1__1bitright), .in2(n1bitshiftright_2__1bitright),
    .in3(n1bitshiftright_3__1bitright), .in4(n1bitshiftright_5__1bitright),
    .in5(n1bitshiftright_4__1bitright), .in6(n1bitshiftright_6__1bitright),
    .in7(n1bitshiftright_7__1bitright), .out(Shifted), .sel(shamt));  // open: en
  _1BitShiftRight u_1bitshiftright_4 (.In(n1bitshiftright_5__1bitright), ._1BitRight(n1bitshiftright_4__1bitright));
  _1BitShiftRight u_1bitshiftright_5 (.In(n1bitshiftright_3__1bitright), ._1BitRight(n1bitshiftright_5__1bitright));
  _1BitShiftRight u_1bitshiftright_6 (.In(n1bitshiftright_4__1bitright), ._1BitRight(n1bitshiftright_6__1bitright));
  _1BitShiftRight u_1bitshiftright_7 (.In(n1bitshiftright_6__1bitright), ._1BitRight(n1bitshiftright_7__1bitright));
endmodule

module _1BitShiftLeft (
  input  [15:0] In,
  output [15:0] _1BitLeft
);

  Multiplexer multiplexer_1 (.in0(In[15]), .in1(In[14]), .out(_1BitLeft[15]), .sel(1'b1));  // open: en
  Multiplexer multiplexer_2 (.in0(In[14]), .in1(In[13]), .out(_1BitLeft[14]), .sel(1'b1));  // open: en
  Multiplexer multiplexer_3 (.in0(In[13]), .in1(In[12]), .out(_1BitLeft[13]), .sel(1'b1));  // open: en
  Multiplexer multiplexer_4 (.in0(In[12]), .in1(In[11]), .out(_1BitLeft[12]), .sel(1'b1));  // open: en
  Multiplexer multiplexer_5 (.in0(In[11]), .in1(In[10]), .out(_1BitLeft[11]), .sel(1'b1));  // open: en
  Multiplexer multiplexer_6 (.in0(In[10]), .in1(In[9]), .out(_1BitLeft[10]), .sel(1'b1));  // open: en
  Multiplexer multiplexer_7 (.in0(In[9]), .in1(In[8]), .out(_1BitLeft[9]), .sel(1'b1));  // open: en
  Multiplexer multiplexer_8 (.in0(In[8]), .in1(In[7]), .out(_1BitLeft[8]), .sel(1'b1));  // open: en
  Multiplexer multiplexer_9 (.in0(In[7]), .in1(In[6]), .out(_1BitLeft[7]), .sel(1'b1));  // open: en
  Multiplexer multiplexer_10 (.in0(In[6]), .in1(In[5]), .out(_1BitLeft[6]), .sel(1'b1));  // open: en
  Multiplexer multiplexer_11 (.in0(In[5]), .in1(In[4]), .out(_1BitLeft[5]), .sel(1'b1));  // open: en
  Multiplexer multiplexer_12 (.in0(In[4]), .in1(In[3]), .out(_1BitLeft[4]), .sel(1'b1));  // open: en
  Multiplexer multiplexer_13 (.in0(In[3]), .in1(In[2]), .out(_1BitLeft[3]), .sel(1'b1));  // open: en
  Multiplexer multiplexer_14 (.in0(In[2]), .in1(In[1]), .out(_1BitLeft[2]), .sel(1'b1));  // open: en
  Multiplexer multiplexer_15 (.in0(In[1]), .in1(In[0]), .out(_1BitLeft[1]), .sel(1'b1));  // open: en
  Multiplexer multiplexer_16 (.in0(In[0]), .in1(1'b0), .out(_1BitLeft[0]), .sel(1'b1));  // open: en
endmodule

module ShiftLeft (
  input  [2:0] shamt,
  input  [15:0] DataIn,
  output [15:0] Shifted
);

  wire [15:0] n1bitshiftleft_1__1bitleft, n1bitshiftleft_2__1bitleft, n1bitshiftleft_3__1bitleft,
       n1bitshiftleft_4__1bitleft, n1bitshiftleft_5__1bitleft, n1bitshiftleft_6__1bitleft,
       n1bitshiftleft_7__1bitleft;

  _1BitShiftLeft u_1bitshiftleft_1 (.In(DataIn), ._1BitLeft(n1bitshiftleft_1__1bitleft));
  _1BitShiftLeft u_1bitshiftleft_2 (.In(n1bitshiftleft_1__1bitleft), ._1BitLeft(n1bitshiftleft_2__1bitleft));
  _1BitShiftLeft u_1bitshiftleft_3 (.In(n1bitshiftleft_2__1bitleft), ._1BitLeft(n1bitshiftleft_3__1bitleft));
  Multiplexer #(.select(3), .width(16)) multiplexer_1 (
    .in0(DataIn), .in1(n1bitshiftleft_1__1bitleft), .in2(n1bitshiftleft_2__1bitleft),
    .in3(n1bitshiftleft_3__1bitleft), .in4(n1bitshiftleft_5__1bitleft), .in5(n1bitshiftleft_4__1bitleft),
    .in6(n1bitshiftleft_6__1bitleft), .in7(n1bitshiftleft_7__1bitleft), .out(Shifted), .sel(shamt));  // open: en
  _1BitShiftLeft u_1bitshiftleft_4 (.In(n1bitshiftleft_5__1bitleft), ._1BitLeft(n1bitshiftleft_4__1bitleft));
  _1BitShiftLeft u_1bitshiftleft_5 (.In(n1bitshiftleft_3__1bitleft), ._1BitLeft(n1bitshiftleft_5__1bitleft));
  _1BitShiftLeft u_1bitshiftleft_6 (.In(n1bitshiftleft_4__1bitleft), ._1BitLeft(n1bitshiftleft_6__1bitleft));
  _1BitShiftLeft u_1bitshiftleft_7 (.In(n1bitshiftleft_6__1bitleft), ._1BitLeft(n1bitshiftleft_7__1bitleft));
endmodule

module PCIncrement (
  input  [15:0] PCIn,
  output [15:0] PCOut
);

  Adder adder_1 (.sub(1'b0), .Result(PCOut), .numA(PCIn), .numB(16'h1));  // open: ovf
endmodule

module Greater (
  input  [15:0] SUBRes,
  output Greater
);

  wire nor_1_out, not_1_out, not_2_out;

  not not_1 (not_1_out, SUBRes[15]);
  nor nor_1 (nor_1_out, SUBRes[0], SUBRes[1], SUBRes[2], SUBRes[3], SUBRes[4], SUBRes[5], SUBRes[6], SUBRes[7], SUBRes[8], SUBRes[9], SUBRes[10], SUBRes[11], SUBRes[12], SUBRes[13], SUBRes[14], SUBRes[15]);
  not not_2 (not_2_out, nor_1_out);
  and and_1 (Greater, not_2_out, not_1_out);
endmodule

module EqualZero (
  input  [15:0] NumIn,
  output AllZero
);

  nor nor_1 (AllZero, NumIn[0], NumIn[1], NumIn[2], NumIn[3], NumIn[4], NumIn[5], NumIn[6], NumIn[7], NumIn[8], NumIn[9], NumIn[10], NumIn[11], NumIn[12], NumIn[13], NumIn[14], NumIn[15]);
endmodule

module BranchPC (
  input  [15:0] PCIn,
  input  [15:0] Immediate,
  output [15:0] PCOut
);

  wire [15:0] adder_2_result;

  Adder adder_1 (.sub(1'b0), .Result(PCOut), .numA(adder_2_result), .numB(16'h1));  // open: ovf
  Adder adder_2 (.sub(1'b0), .Result(adder_2_result), .numA(PCIn), .numB(Immediate));  // open: ovf
endmodule

module JumpAddress (
  input  [11:0] _12BitAddress,
  input  [15:0] PCIn,
  output [15:0] PCOut
);


  assign PCOut = {PCIn[15:12], _12BitAddress};
endmodule

module Lower7Bits (
  input  [15:0] DataToPrint,
  output [6:0] ASCII
);


  assign ASCII = DataToPrint[6:0];
endmodule

module KeyboardInput (
  input  [6:0] Keyboard,
  input  available,
  output [15:0] out_3
);

  and and_1 (out_3[0], Keyboard[0], available);
  and and_2 (out_3[1], Keyboard[1], available);
  and and_3 (out_3[2], Keyboard[2], available);
  and and_4 (out_3[3], Keyboard[3], available);
  and and_5 (out_3[4], Keyboard[4], available);
  and and_6 (out_3[5], Keyboard[5], available);
  and and_7 (out_3[6], Keyboard[6], available);
  not not_1 (out_3[7], available);

  assign out_3[15:8] = {8{1'b0}};
endmodule

module InstructionDecoder (
  input  [15:0] Instruction,
  output [2:0] shamt,
  output [2:0] rd,
  output [2:0] rt,
  output [2:0] rs,
  output [3:0] opcode,
  output [5:0] immediate,
  output [11:0] address
);


  assign address = Instruction[11:0];
  assign immediate = Instruction[5:0];
  assign opcode = Instruction[15:12];
  assign rd = Instruction[5:3];
  assign rs = Instruction[11:9];
  assign rt = Instruction[8:6];
  assign shamt = Instruction[2:0];

  // Other names for the same wires on the sheet: in0 = Instruction[0]; in1 = Instruction[1]; in2 = Instruction[2];
  //   in3 = Instruction[3]; in4 = Instruction[4]; in5 = Instruction[5]; in6 = Instruction[6]; in7 = Instruction[7];
  //   in8 = Instruction[8]; in9 = Instruction[9]; in10 = Instruction[10]; in11 = Instruction[11];
  //   in12 = Instruction[12]; in13 = Instruction[13]; in14 = Instruction[14]; in15 = Instruction[15]
endmodule

module OpcodeDecoder (
  input  [3:0] opcode,
  output Input,
  output WE,
  output Output,
  output Rdst,
  output DMwe,
  output Rwd,
  output ALUinB,
  output Br,
  output Jp,
  output [2:0] ALUop,
  output Jr,
  output Beqz,
  output Jal,
  output Bgt
);

  wire and_1_out, and_2_out, and_3_out, and_4_out, and_5_out, and_6_out, and_7_out, and_8_out, and_9_out,
       and_10_out, and_11_out, and_12_out, and_13_out, and_14_out, and_15_out, and_16_out, and_17_out,
       and_20_out, and_21_out, not_1_out, not_2_out, not_3_out, not_4_out, not_5_out, not_6_out, not_7_out,
       not_8_out, not_9_out, not_10_out, not_11_out, not_12_out, not_13_out, not_14_out, not_15_out,
       not_16_out, not_17_out, not_18_out, not_19_out, not_20_out, not_21_out, not_22_out, not_23_out,
       not_24_out, not_25_out, not_26_out, not_27_out, not_28_out, not_29_out, not_30_out, not_31_out,
       not_32_out, not_33_out, not_34_out, not_35_out, not_36_out, not_37_out, not_38_out, not_39_out,
       not_40_out, not_41_out;

  not not_1 (not_1_out, opcode[3]);
  not not_2 (not_2_out, opcode[2]);
  not not_3 (not_3_out, opcode[1]);
  not not_4 (not_4_out, opcode[0]);
  not not_5 (not_5_out, opcode[3]);
  not not_6 (not_6_out, opcode[2]);
  not not_7 (not_7_out, opcode[1]);
  not not_8 (not_8_out, opcode[0]);
  not not_9 (not_9_out, opcode[3]);
  not not_10 (not_10_out, opcode[2]);
  not not_11 (not_11_out, opcode[1]);
  not not_12 (not_12_out, opcode[0]);
  not not_13 (not_13_out, opcode[3]);
  not not_14 (not_14_out, opcode[2]);
  not not_15 (not_15_out, opcode[1]);
  not not_16 (not_16_out, opcode[0]);
  not not_17 (not_17_out, opcode[3]);
  not not_18 (not_18_out, opcode[1]);
  not not_19 (not_19_out, opcode[0]);
  not not_20 (not_20_out, opcode[1]);
  and and_1 (and_1_out, not_1_out, not_2_out, opcode[1], not_4_out);
  and and_2 (and_2_out, opcode[3], not_2_out, not_3_out, opcode[0]);
  and and_3 (and_3_out, not_5_out, not_6_out, opcode[1], not_8_out);
  and and_4 (and_4_out, opcode[3], not_6_out, not_7_out, opcode[0]);
  and and_5 (and_5_out, opcode[3], not_6_out, opcode[1], not_8_out);
  and and_6 (and_6_out, not_9_out, not_10_out, not_11_out, opcode[0]);
  and and_7 (and_7_out, opcode[3], not_10_out, not_11_out, not_12_out);
  and and_8 (and_8_out, not_9_out, opcode[2], not_12_out);
  and and_9 (and_9_out, not_9_out, opcode[2], opcode[1]);
  and and_10 (and_10_out, not_13_out, not_14_out, not_15_out, not_16_out);
  and and_11 (and_11_out, not_13_out, not_14_out, not_15_out, opcode[0]);
  and and_12 (and_12_out, not_17_out, opcode[2], not_18_out, opcode[0]);
  and and_13 (and_13_out, not_17_out, opcode[2], opcode[1], not_19_out);
  and and_14 (and_14_out, opcode[3], opcode[2], opcode[0]);
  not not_21 (not_21_out, opcode[3]);
  and and_15 (and_15_out, not_21_out, not_22_out);
  not not_22 (not_22_out, opcode[2]);
  not not_23 (not_23_out, opcode[3]);
  and and_16 (and_16_out, not_23_out, not_24_out);
  not not_24 (not_24_out, opcode[0]);
  and and_17 (and_17_out, not_20_out, opcode[0]);
  or or_1 (ALUop[1], and_10_out, and_11_out);
  or or_2 (ALUop[2], and_12_out, and_13_out);
  or or_3 (Rdst, and_1_out, and_2_out);
  or or_4 (ALUinB, and_3_out, and_4_out, and_5_out);
  or or_5 (ALUop[0], and_6_out, and_7_out, and_8_out, and_9_out);
  or or_6 (WE, and_14_out, and_15_out, and_16_out, and_17_out);
  not not_25 (not_25_out, opcode[2]);
  and and_18 (DMwe, opcode[3], not_25_out, opcode[1], not_26_out);
  not not_26 (not_26_out, opcode[0]);
  not not_27 (not_27_out, opcode[2]);
  and and_19 (Rwd, opcode[3], not_27_out, not_28_out, opcode[0]);
  not not_28 (not_28_out, opcode[1]);
  not not_29 (not_29_out, opcode[3]);
  not not_30 (not_30_out, opcode[2]);
  not not_31 (not_31_out, opcode[1]);
  not not_32 (not_32_out, opcode[0]);
  and and_20 (and_20_out, not_29_out, opcode[2], opcode[1], opcode[0]);
  and and_21 (and_21_out, opcode[3], not_30_out, not_31_out, not_32_out);
  not not_33 (not_33_out, opcode[2]);
  not not_34 (not_34_out, opcode[1]);
  not not_35 (not_35_out, opcode[0]);
  not not_36 (not_36_out, opcode[1]);
  not not_37 (not_37_out, opcode[0]);
  or or_7 (Br, and_20_out, and_21_out);
  and and_22 (Jp, opcode[3], not_33_out, opcode[1], opcode[0]);
  and and_23 (Jr, opcode[3], opcode[2], not_34_out, not_35_out);
  and and_24 (Jal, opcode[3], opcode[2], not_36_out, opcode[0]);
  and and_25 (Input, opcode[3], opcode[2], opcode[1], opcode[0]);
  and and_26 (Output, opcode[3], opcode[2], opcode[1], not_37_out);
  not not_38 (not_38_out, opcode[2]);
  not not_39 (not_39_out, opcode[1]);
  not not_40 (not_40_out, opcode[0]);
  not not_41 (not_41_out, opcode[3]);
  and and_27 (Beqz, opcode[3], not_38_out, not_39_out, not_40_out);
  and and_28 (Bgt, not_41_out, opcode[2], opcode[1], opcode[0]);

  // Other names for the same wires on the sheet: op1 = opcode[0]; op2 = opcode[1]; op3 = opcode[2]; op4 = opcode[3]
endmodule

module PCRegister (
  input  clk,
  input  rst,
  input  [15:0] dataIn,
  output [15:0] dataOut
);

  D_Flip_Flop #(.trigger("falling")) d_ff_1 (
    .clk(clk), .D(dataIn[0]), .Q(dataOut[0]), .reset(rst));  // open: Qn, preset, en
  D_Flip_Flop #(.trigger("falling")) d_ff_2 (
    .clk(clk), .D(dataIn[1]), .Q(dataOut[1]), .reset(rst));  // open: Qn, preset, en
  D_Flip_Flop #(.trigger("falling")) d_ff_3 (
    .clk(clk), .D(dataIn[2]), .Q(dataOut[2]), .reset(rst));  // open: Qn, preset, en
  D_Flip_Flop #(.trigger("falling")) d_ff_4 (
    .clk(clk), .D(dataIn[3]), .Q(dataOut[3]), .reset(rst));  // open: Qn, preset, en
  D_Flip_Flop #(.trigger("falling")) d_ff_5 (
    .clk(clk), .D(dataIn[4]), .Q(dataOut[4]), .reset(rst));  // open: Qn, preset, en
  D_Flip_Flop #(.trigger("falling")) d_ff_6 (
    .clk(clk), .D(dataIn[5]), .Q(dataOut[5]), .reset(rst));  // open: Qn, preset, en
  D_Flip_Flop #(.trigger("falling")) d_ff_7 (
    .clk(clk), .D(dataIn[6]), .Q(dataOut[6]), .reset(rst));  // open: Qn, preset, en
  D_Flip_Flop #(.trigger("falling")) d_ff_8 (
    .clk(clk), .D(dataIn[7]), .Q(dataOut[7]), .reset(rst));  // open: Qn, preset, en
  D_Flip_Flop #(.trigger("falling")) d_ff_9 (
    .clk(clk), .D(dataIn[8]), .Q(dataOut[8]), .reset(rst));  // open: Qn, preset, en
  D_Flip_Flop #(.trigger("falling")) d_ff_10 (
    .clk(clk), .D(dataIn[9]), .Q(dataOut[9]), .reset(rst));  // open: Qn, preset, en
  D_Flip_Flop #(.trigger("falling")) d_ff_11 (
    .clk(clk), .D(dataIn[10]), .Q(dataOut[10]), .reset(rst));  // open: Qn, preset, en
  D_Flip_Flop #(.trigger("falling")) d_ff_12 (
    .clk(clk), .D(dataIn[11]), .Q(dataOut[11]), .reset(rst));  // open: Qn, preset, en
  D_Flip_Flop #(.trigger("falling")) d_ff_13 (
    .clk(clk), .D(dataIn[12]), .Q(dataOut[12]), .reset(rst));  // open: Qn, preset, en
  D_Flip_Flop #(.trigger("falling")) d_ff_14 (
    .clk(clk), .D(dataIn[13]), .Q(dataOut[13]), .reset(rst));  // open: Qn, preset, en
  D_Flip_Flop #(.trigger("falling")) d_ff_15 (
    .clk(clk), .D(dataIn[14]), .Q(dataOut[14]), .reset(rst));  // open: Qn, preset, en
  D_Flip_Flop #(.trigger("falling")) d_ff_16 (
    .clk(clk), .D(dataIn[15]), .Q(dataOut[15]), .reset(rst));  // open: Qn, preset, en
endmodule
